// Logisim project singleCycleCPU.circ as structural Verilog: 4 circuits, main circuit main
module main (
);

  wire _1Reg, _2Reg, _3Reg, clock_1_out, clock_2_out, clock_3_out, clock_4_out, clock_5_out, clock_6_out,
       clock_7_out, clock_8_out, clock_9_out, clock_10_out, clock_11_out, clock_12_out, clock_13_out,
       clock_14_out, clock_15_out, clock_16_out, clock_17_out, clock_18_out, clock_19_out, clock_20_out,
       ctrl_unit_1_memoryread, ctrl_unit_1_memroywrite, ctrl_unit_1_regwrite, EX_2_q, EX_4_q, MemoryRead,
       MemoryWrite, Zero;
  wire [1:0] BusBSrc, BusWSrc, ctrl_unit_1_buswsrc, Ex_5_q, EX_q, FA, FB, pcctrl_1_out_3;
  wire [3:0] ALUOP, EX_6_q;
  wire [4:0] imm16, rd2, rd3, rd4, rd___imm5l, rs1;
  wire [5:0] opcode;
  wire [10:0] f___imm11u;
  wire [15:0] register_1_q;
  wire [19:0] adder_3_out, bit_extender_1_out, Branch_Target, BTarget, Jump_Target, multiplexer_1_out, NPC_q,
       PC___1, PC_q;
  wire [31:0] _1, _2, _3, A_q, B_q, bit_extender_2_out, bit_extender_3_out, bit_extender_4_out,
       bit_extender_6_out, D_q, multiplexer_2_out, R_q, Ra, ram_1_data, Rb, register_2_q, register_3_q,
       register_4_q, register_file_1_busa, register_file_1_busb, rom_1_data;

  Register #(.width(16)) register_1 (.D({f___imm11u, imm16}), .Q(register_1_q), .clk(clock_1_out));  // open: en, clr
  Clock clock_1 (.out(clock_1_out));
  Adder #(.width(20)) adder_1 (.a(20'h1), .b(PC_q), .out(PC___1));  // open: cin, cout
  Multiplexer #(.select(2), .width(20), .enable("false")) multiplexer_1 (
    .in0(PC___1), .in1(Jump_Target), .in2(Branch_Target), .in3({20{1'b0}}), .out(multiplexer_1_out),
    .sel(pcctrl_1_out_3));
  PcCtrl pcctrl_1 (.OpCode(opcode), .out_3(pcctrl_1_out_3), .ZeroFlag(Zero));
  assign bit_extender_1_out = {{4{register_1_q[15]}}, register_1_q};  // Bit_Extender bit_extender_1
  Register #(.width(20)) PC (.D(multiplexer_1_out), .Q(PC_q), .clk(clock_2_out));  // open: en, clr
  Clock clock_2 (.out(clock_2_out));
  Adder #(.width(20)) adder_2 (.a(bit_extender_1_out), .b(Ra[19:0]), .out(Jump_Target));  // open: cin, cout
  Adder #(.width(20)) adder_3 (.a(NPC_q), .b(BTarget), .out(adder_3_out));  // open: cin, cout
  Register #(.width(20)) NPC (.D(PC_q), .Q(NPC_q), .clk(clock_3_out));  // open: en, clr
  Clock clock_3 (.out(clock_3_out));
  Register #(.width(20)) BTA (.D(adder_3_out), .Q(Branch_Target), .clk(clock_4_out));  // open: en, clr
  Clock clock_4 (.out(clock_4_out));
  Register #(.width(2)) MEM (.D(EX_q), .Q(BusWSrc), .clk(clock_5_out));  // open: en, clr
  Register #(.width(2)) EX (.D(ctrl_unit_1_buswsrc), .Q(EX_q), .clk(clock_5_out));  // open: en, clr
  Clock clock_5 (.out(clock_5_out));
  Register #(.width(1)) EX_2 (.D(ctrl_unit_1_memroywrite), .Q(EX_2_q), .clk(clock_6_out));  // open: en, clr
  Clock clock_6 (.out(clock_6_out));
  ROM #(.addrWidth(20), .dataWidth(32)) rom_1 (.addr(PC_q), .data(rom_1_data), .sel(1'b1));
  Clock clock_7 (.out(clock_7_out));
  Hazard_Detection___Forward HAZARD (
    .Rs(rs1), .Rt(imm16), .Rd2(rd2), .Rd3(rd3), .Rd4(rd4), .EX_RegWrite(_1Reg), .MEM_RegWrite(_2Reg),
    .WB_RegWrite(_3Reg), .ForwardA(FA), .ForwardB(FB));
  ctrl_unit ctrl_unit_1 (
    .in_1(opcode), .MemroyWrite(ctrl_unit_1_memroywrite), .BusWSrc(ctrl_unit_1_buswsrc),
    .RegWrite(ctrl_unit_1_regwrite), .BusBSrc(BusBSrc), .MemoryRead(ctrl_unit_1_memoryread));
  Register #(.width(1)) MEM_2 (.D(EX_2_q), .Q(MemoryWrite), .clk(clock_6_out));  // open: en, clr
  Register #(.width(32)) inst (
    .D(rom_1_data), .Q({f___imm11u, imm16, rs1, rd___imm5l, opcode}), .clk(clock_7_out));  // open: en, clr
  Register #(.width(1)) EX_3 (.D(ctrl_unit_1_regwrite), .Q(_1Reg), .clk(clock_9_out));  // open: en, clr
  Register #(.width(1)) EX_4 (.D(ctrl_unit_1_memoryread), .Q(EX_4_q), .clk(clock_8_out));  // open: en, clr
  Clock clock_8 (.out(clock_8_out));
  // Probe on {f___imm11u, imm16}
  // Probe on opcode
  // Probe on f___imm11u
  Register #(.width(1)) MEM_3 (.D(_1Reg), .Q(_2Reg), .clk(clock_9_out));  // open: en, clr
  Clock clock_9 (.out(clock_9_out));
  Register #(.width(1)) MEM_4 (.D(EX_4_q), .Q(MemoryRead), .clk(clock_8_out));  // open: en, clr
  Register #(.width(5)) u_Rd2 (.D(rd___imm5l), .Q(rd2), .clk(clock_10_out));  // open: en, clr
  Clock clock_10 (.out(clock_10_out));
  // Probe on rd___imm5l
  // Probe on rs1
  // Probe on imm16
  Register #(.width(1)) WB (.D(_2Reg), .Q(_3Reg), .clk(clock_9_out));  // open: en, clr
  Register #(.width(5)) u_Rd4 (.D(rd3), .Q(rd4), .clk(clock_10_out));  // open: en, clr
  Register #(.width(5)) u_Rd3 (.D(rd2), .Q(rd3), .clk(clock_10_out));  // open: en, clr
  // Probe on _3
  assign bit_extender_2_out = {{16{f___imm11u[10]}}, {f___imm11u, imm16}};  // Bit_Extender bit_extender_2
  Clock clock_11 (.out(clock_11_out));
  assign bit_extender_3_out = {{16{1'b0}}, {f___imm11u, imm16}};  // Bit_Extender bit_extender_3
  Clock clock_12 (.out(clock_12_out));
  register_file register_file_1 (
    .RA(rs1), .RB(imm16), .RegWrite(_3Reg), .RW(rd4), .BusW(_3), .BusB(register_file_1_busb),
    .BusA(register_file_1_busa));
  Register #(.width(32)) A (.D(register_file_1_busa), .Q(A_q), .clk(clock_13_out));  // open: en, clr
  Clock clock_13 (.out(clock_13_out));
  Register #(.width(32)) B (.D(register_file_1_busb), .Q(B_q), .clk(clock_14_out));  // open: en, clr
  Clock clock_14 (.out(clock_14_out));
  Register #(.width(32)) register_2 (.D(bit_extender_2_out), .Q(register_2_q), .clk(clock_11_out));  // open: en, clr
  Register #(.width(32)) register_3 (.D(bit_extender_3_out), .Q(register_3_q), .clr(clock_12_out));  // open: en, clk
  assign bit_extender_4_out = {{16{f___imm11u[10]}}, {f___imm11u, rd___imm5l}};  // Bit_Extender bit_extender_4
  Multiplexer #(.select(2), .width(32), .enable("false")) multiplexer_2 (
    .in0(Rb), .in1(register_2_q), .in2(register_3_q), .in3(register_4_q), .out(multiplexer_2_out),
    .sel(Ex_5_q));
  // Probe on Ex_5_q
  Register #(.width(2)) Ex_5 (.D(BusBSrc), .Q(Ex_5_q), .clk(clock_15_out));  // open: en, clr
  Register #(.width(32)) register_4 (.D(bit_extender_4_out), .Q(register_4_q), .clk(clock_16_out));  // open: en, clr
  Clock clock_15 (.out(clock_15_out));
  Clock clock_16 (.out(clock_16_out));
  assign BTarget = {{4{f___imm11u[10]}}, {f___imm11u, rd___imm5l}};  // Bit_Extender bit_extender_5
  // Probe on Ra
  Multiplexer #(.select(2), .width(32), .enable("false")) multiplexer_3 (
    .in0(A_q), .in1(_1), .in2(_2), .in3(_3), .out(Ra), .sel(FA));
  Multiplexer #(.select(2), .width(32), .enable("false")) multiplexer_4 (
    .in0(B_q), .in1(_1), .in2(_2), .in3(_3), .out(Rb), .sel(FB));
  // Probe on bit_extender_4_out
  Register #(.width(4)) EX_6 (.D(ALUOP), .Q(EX_6_q), .clk(clock_17_out));  // open: en, clr
  Clock clock_17 (.out(clock_17_out));
  // Probe on EX_6_q
  ALU alu_1 (.A(Ra), .ALUOP(EX_6_q), .ALU_OUTPUT(_1), .B(multiplexer_2_out), .ZeroFlag(Zero));
  // Probe on _1
  Register #(.width(32)) R (.D(_1), .Q(R_q), .clk(clock_18_out));  // open: en, clr
  Register #(.width(32)) D (.D(Rb), .Q(D_q), .clk(clock_18_out));  // open: en, clr
  Clock clock_18 (.out(clock_18_out));
  ALUCtrl aluctrl_1 (.FunctoinCode(f___imm11u), .OpCode(opcode), .ALUOp(ALUOP));
  assign bit_extender_6_out = {{12{1'b0}}, PC___1};  // Bit_Extender bit_extender_6
  // Probe on MemoryWrite
  Clock clock_19 (.out(clock_19_out));
  RAM #(.addrWidth(20), .dataWidth(32), .bus("separate")) ram_1 (
    .addr(R_q[19:0]), .din(D_q), .data(ram_1_data), .str(MemoryWrite), .clk(clock_19_out), .ld(MemoryRead));  // open: sel, clr
  // Probe on MemoryRead
  Multiplexer #(.select(2), .width(32), .enable("false")) multiplexer_5 (
    .in0(R_q), .in1(ram_1_data), .in2(bit_extender_6_out), .in3({32{1'b0}}), .out(_2), .sel(BusWSrc));
  Register #(.width(32)) Data (.D(_2), .Q(_3), .clk(clock_20_out));  // open: en, clr
  // Probe on BusWSrc
  Clock clock_20 (.out(clock_20_out));

  // Other names for the same wires on the sheet: rs2[4:0] = imm16; imm16[15:5] = f___imm11u; regWrite = _3Reg;
  //   WBbusW[31:0] = _3

  // Notes on the sheet:
  //   contents of rom_1 (hex, n*v repeats v):
  //   10045 20085 300c5 40105 50145
  //   imm16s
  //   imm16z
  //   busB
  //   imm11,5s
endmodule

module ctrl_unit (
  input  [5:0] in_1,
  output RegWrite,
  output [1:0] BusBSrc,
  output MemroyWrite,
  output MemoryRead,
  output [1:0] BusWSrc
);

  ROM #(.addrWidth(6), .dataWidth(7)) rom_1 (
    .addr(in_1), .data({RegWrite, BusBSrc, MemroyWrite, MemoryRead, BusWSrc}));  // open: sel

  // Notes on the sheet:
  //   opCode
  //   contents of rom_1 (hex, n*v repeats v):
  //   40 4*60 50 50 50 4*60 50 52 55 38
endmodule

module PcCtrl (
  input  [5:0] OpCode,
  input  ZeroFlag,
  output [1:0] out_3
);

  wire and_1_out, clock_1_out;

  and and_1 (and_1_out, ZeroFlag, OpCode[4]);
  Register #(.width(1)) register_1 (.D(and_1_out), .Q(out_3[1]), .clk(clock_1_out));  // open: en, clr
  Clock clock_1 (.out(clock_1_out));
  and and_2 (out_3[0], OpCode[3], OpCode[2], ~OpCode[1], OpCode[0]);  // AND_Gate
endmodule

module Hazard_Detection___Forward (
  input  EX_RegWrite,
  input  MEM_RegWrite,
  input  WB_RegWrite,
  input  [4:0] Rs,
  input  [4:0] Rt,
  input  [4:0] Rd2,
  input  [4:0] Rd3,
  input  [4:0] Rd4,
  output [1:0] ForwardA,
  output [1:0] ForwardB
);

  wire comparator_1_eq, comparator_2_eq, comparator_3_eq, comparator_4_eq, comparator_5_eq, comparator_6_eq,
       fa1, fa2, fa3, fb1, fb2, fb3;

  Comparator #(.width(5)) comparator_1 (.a(Rs), .b(Rd2), .eq(comparator_1_eq));  // open: gt, lt
  Comparator #(.width(5)) comparator_2 (.a(Rs), .b(Rd3), .eq(comparator_2_eq));  // open: gt, lt
  Comparator #(.width(5)) comparator_3 (.a(Rs), .b(Rd4), .eq(comparator_3_eq));  // open: gt, lt
  Comparator #(.width(5)) comparator_4 (.a(Rt), .b(Rd2), .eq(comparator_4_eq));  // open: gt, lt
  Comparator #(.width(5)) comparator_5 (.a(Rt), .b(Rd3), .eq(comparator_5_eq));  // open: gt, lt
  Comparator #(.width(5)) comparator_6 (.a(Rt), .b(Rd4), .eq(comparator_6_eq));  // open: gt, lt
  and and_1 (fa1, EX_RegWrite, comparator_1_eq);
  and and_2 (fa2, MEM_RegWrite, comparator_2_eq);
  and and_3 (fa3, WB_RegWrite, comparator_3_eq);
  and and_4 (fb1, EX_RegWrite, comparator_4_eq);
  and and_5 (fb2, MEM_RegWrite, comparator_5_eq);
  and and_6 (fb3, WB_RegWrite, comparator_6_eq);
  or or_1 (ForwardA[0], fa1, fa3);
  or or_2 (ForwardA[1], fa2, fa3);
  or or_3 (ForwardB[0], fb1, fb3);
  or or_4 (ForwardB[1], fb2, fb3);

  // Other names for the same wires on the sheet: exReg = EX_RegWrite; memReg = MEM_RegWrite; wbReg = WB_RegWrite
endmodule
