// Logisim project Pipeline3.circ as structural Verilog: 7 circuits, main circuit main
module main (
  input  in_1,
  input  in_2
);

  wire Branch, branchd, clock_1_out, Forward_Hazard_stall, JALR, Kill1, Kill2, MemRd, MemWr, not_1_out,
       not_2_out, or_1_out, RegWR, RegWRP;
  wire [1:0] AluSrc, FA, FB, pc_ctrl_1_pcsrc, WbData;
  wire [3:0] alu_ctrl_1_aluop;
  wire [4:0] imm5L, imm16, MEM_q, rd, Rd2, Rd3, rs1;
  wire [5:0] opcode;
  wire [10:0] EX_q, f;
  wire [11:0] multiplexer_5_out;
  wire [11:11] Forward_Hazard_branchd;
  wire [19:0] adder_2_out, adder_3_out, BranchAdrees, BTA_q, multiplexer_1_out, NPC_q, register_1_q;
  wire [31:0] adder_1_out, ALU_result, bit_extender_1_out, bit_extender_2_out, bit_extender_5_out, D_q,
       Imm_q, ImmLU_q, ImmS_q, Jimm, Mdata, multiplexer_2_out, multiplexer_3_out, multiplexer_4_out,
       multiplexer_6_out, R_q, Ra, ram_1_data, Rb, Register_2_busa, Register_2_busb, rom_1_data, Write;

  Adder #(.width(32)) adder_1 (.a(Ra), .b(Jimm), .out(adder_1_out));  // open: cin, cout
  PC_Ctrl pc_ctrl_1 (.JALR(JALR), .branchd(branchd), .PCsrc(pc_ctrl_1_pcsrc), .Kill1(Kill1), .Kill2(Kill2));
  Clock clock_1 (.out(clock_1_out));
  Path_Ctrl path_ctrl_1 (
    .opcode(opcode), .WbData(WbData), .RegWr(RegWR), .AluSrc(AluSrc), .MemWr(MemWr), .MemRd(MemRd));
  Multiplexer #(.select(2), .width(20), .enable("false")) multiplexer_1 (
    .in0(adder_2_out), .in1(adder_1_out[19:0]), .in2(BTA_q), .out(multiplexer_1_out), .sel(pc_ctrl_1_pcsrc));  // open: in3
  not not_1 (not_1_out, Forward_Hazard_stall);
  Register_part #(.width(20)) register_1 (
    .D(multiplexer_1_out), .en(not_1_out), .Q(register_1_q), .clk(clock_1_out), .clr(in_2));
  Adder #(.width(20)) adder_2 (.a(20'h1), .b(register_1_q), .out(adder_2_out));  // open: cin, cout
  not not_2 (not_2_out, Forward_Hazard_stall);
  ROM #(.addrWidth(20), .dataWidth(32)) rom_1 (.addr(register_1_q), .data(rom_1_data), .sel(not_2_out));
  Register_part #(.width(20)) NPC (.D(register_1_q), .Q(NPC_q), .clk(clock_1_out));  // open: en, clr
  Multiplexer #(.width(32), .enable("false")) multiplexer_2 (
    .in0(rom_1_data), .in1({32{1'b0}}), .out(multiplexer_2_out), .sel(Kill1));
  Register_part #(.width(32)) Inst (
    .D(multiplexer_2_out), .Q({f, imm16, rs1, imm5L, opcode}), .clk(clock_1_out));  // open: en, clr
  assign bit_extender_1_out = {{12{adder_2_out[19]}}, adder_2_out};  // Bit_Extender bit_extender_1
  assign bit_extender_2_out = {{16{1'b0}}, {f, imm16}};  // Bit_Extender bit_extender_2
  assign Jimm = {{16{f[10]}}, {f, imm16}};  // Bit_Extender bit_extender_3
  assign BranchAdrees = {{4{f[10]}}, {f, imm5L}};  // Bit_Extender bit_extender_4
  assign bit_extender_5_out = {{16{f[10]}}, {f, imm5L}};  // Bit_Extender bit_extender_5
  ALU_Ctrl alu_ctrl_1 (.f(f[3:0]), .opcode(opcode[4:0]), .ALUop(alu_ctrl_1_aluop));
  Adder #(.width(20)) adder_3 (.a(NPC_q), .b(BranchAdrees), .out(adder_3_out));  // open: cin, cout
  Register_part #(.width(5)) u_RD2 (.D(imm5L), .Q(Rd2), .clk(clock_1_out));  // open: en, clr
  Register Register_2 (
    .RA(rs1), .RB(imm16), .RW(rd), .CLR(in_1), .BusW(Write), .RegWrite(RegWRP), .Clock(clock_1_out),
    .BusA(Register_2_busa), .BusB(Register_2_busb));
  Register_part #(.width(32)) Imm (.D(bit_extender_2_out), .Q(Imm_q), .clk(clock_1_out));  // open: en, clr
  or or_1 (or_1_out, Kill2, Forward_Hazard_stall);
  Register_part #(.width(32)) ImmS (.D(Jimm), .Q(ImmS_q), .clk(clock_1_out));  // open: en, clr
  Register_part #(.width(32)) ImmLU (.D(bit_extender_5_out), .Q(ImmLU_q), .clk(clock_1_out));  // open: en, clr
  Multiplexer #(.select(2), .width(32), .enable("false")) multiplexer_3 (
    .in0(Register_2_busa), .in1(ALU_result), .in2(Mdata), .in3(Write), .out(multiplexer_3_out), .sel(FA));
  Register_part #(.width(32)) A (.D(multiplexer_3_out), .Q(Ra), .clk(clock_1_out));  // open: en, clr
  Register_part #(.width(32)) B (.D(multiplexer_4_out), .Q(Rb), .clk(clock_1_out));  // open: en, clr
  Multiplexer #(.select(2), .width(32), .enable("false")) multiplexer_4 (
    .in0(Register_2_busb), .in1(ALU_result), .in2(Mdata), .in3(Write), .out(multiplexer_4_out), .sel(FB));
  Register_part #(.width(12)) EX (.D(multiplexer_5_out), .Q({branchd, EX_q}), .clk(clock_1_out));  // open: en, clr
  Multiplexer #(.width(12), .enable("false")) multiplexer_5 (
    .in0({Forward_Hazard_branchd[11], WbData, RegWR, MemRd, MemWr, alu_ctrl_1_aluop, AluSrc}),
    .in1({12{1'b0}}), .out(multiplexer_5_out), .sel(or_1_out));
  Forward_Hazard Forward_Hazard (
    .Stall(Forward_Hazard_stall), .opcode(opcode), .rs1(rs1), .rs2(imm16), .FA(FA), .FB(FB), .Branch(Branch),
    .rd2(Rd2), .rd3(Rd3), .rd4(rd), .EXMEMRD(EX_q[7]), .EXWR(EX_q[8]), .MEMWR(MEM_q[2]), .WBWR(RegWRP),
    .JALR(JALR), .branchd(Forward_Hazard_branchd[11]));
  Register_part #(.width(20)) BTA (.D(adder_3_out), .Q(BTA_q), .clk(clock_1_out));  // open: en, clr
  ALU ALU (._1(Ra), ._2(multiplexer_6_out), .ALUOP(EX_q[5:2]), .out_5(Branch), .Result(ALU_result));
  Register_part #(.width(5)) u_RD3 (.D(Rd2), .Q(Rd3), .clk(clock_1_out));  // open: en, clr
  Register_part #(.width(32)) R (.D(ALU_result), .Q(R_q), .clk(clock_1_out));  // open: en, clr
  Multiplexer #(.select(2), .width(32), .enable("false")) multiplexer_6 (
    .in0(Rb), .in1(Imm_q), .in2(ImmS_q), .in3(ImmLU_q), .out(multiplexer_6_out), .sel(EX_q[1:0]));
  Register_part #(.width(32)) D (.D(Rb), .Q(D_q), .clk(clock_1_out));  // open: en, clr
  Register_part #(.width(5)) MEM (.D(EX_q[10:6]), .Q(MEM_q), .clk(clock_1_out));  // open: en, clr
  RAM #(.addrWidth(20), .dataWidth(32), .bus("separate")) ram_1 (
    .addr(R_q[19:0]), .din(D_q), .data(ram_1_data), .str(MEM_q[0]), .clk(clock_1_out), .ld(MEM_q[1]));  // open: sel, clr
  Multiplexer #(.select(2), .width(32), .enable("false")) multiplexer_7 (
    .in0(R_q), .in1(ram_1_data), .in2(bit_extender_1_out), .out(Mdata), .sel(MEM_q[4:3]));  // open: in3
  Register_part #(.width(32)) Data (.D(Mdata), .Q(Write), .clk(clock_1_out));  // open: en, clr
  Register_part #(.width(1)) WB (.D(MEM_q[2]), .Q(RegWRP), .clk(clock_1_out));  // open: en, clr
  Register_part #(.width(5)) RD4 (.D(Rd3), .Q(rd), .clk(clock_1_out));  // open: en, clr

  // Other names for the same wires on the sheet: rs2[4:0] = imm16; imm11U[10:0] = f; imm16[15:5] = f; Rd4[4:0] = rd

  // Notes on the sheet:
  //   contents of rom_1 (hex, n*v repeats v):
  //   60845 81085 5*32105 20990 5*218c5 718c5
endmodule

module ALU (
  input  [31:0] _1,
  input  [31:0] _2,
  input  [3:0] ALUOP,
  output [31:0] Result,
  output out_5
);

  wire BEQ, BGE, BGEU, BLT, BLTU, BNE, comparator_1_lt, comparator_2_lt;
  wire [31:0] ADD, AND, bit_extender_3_out, LUI, MUL, NOR, OR, ROR, SLL, SLT, SLTU, SRA, SRL, SUB, XOR;

  Shifter #(.width(32)) shifter_1 (.in(_1), .\dist (_2[4:0]), .out(SLL));
  Shifter #(.width(32), .shift("lr")) shifter_2 (.in(_1), .\dist (_2[4:0]), .out(SRL));
  Shifter #(.width(32), .shift("ar")) shifter_3 (.in(_1), .\dist (_2[4:0]), .out(SRA));
  Shifter #(.width(32), .shift("rr")) shifter_4 (.in(_1), .\dist (_2[4:0]), .out(ROR));
  Adder #(.width(32)) adder_1 (.a(_1), .b(_2), .out(ADD));  // open: cin, cout
  Subtractor #(.width(32)) subtractor_1 (.a(_1), .b(_2), .out(SUB));  // open: bin, bout
  Comparator #(.width(32)) comparator_1 (.a(_1), .b(_2), .lt(comparator_1_lt));  // open: gt, eq
  assign SLT = {{31{1'b0}}, comparator_1_lt};  // Bit_Extender bit_extender_1
  Comparator #(.width(32), .mode("unsigned")) comparator_2 (.a(_1), .b(_2), .lt(comparator_2_lt));  // open: gt, eq
  assign SLTU = {{31{1'b0}}, comparator_2_lt};  // Bit_Extender bit_extender_2
  assign XOR = _1 ^ _2;  // XOR_Gate xor_1, 32 bits wide
  assign OR = _1 | _2;  // OR_Gate or_1, 32 bits wide
  assign AND = _1 & _2;  // AND_Gate and_1, 32 bits wide
  assign NOR = ~(_1 | _2);  // NOR_Gate nor_1, 32 bits wide
  Multiplier #(.width(32)) multiplier_1 (.a(_1), .b(_2), .out(MUL));  // open: cin, cout
  assign bit_extender_3_out = {{16{1'b0}}, _2[15:0]};  // Bit_Extender bit_extender_3
  Shifter #(.width(32)) shifter_5 (.in(bit_extender_3_out), .\dist ({5{1'b1}}), .out(LUI));
  Comparator #(.width(32)) comparator_3 (.a(_1), .b(_2), .eq(BEQ));  // open: gt, lt
  Comparator #(.width(32)) comparator_4 (.a(_1), .b(_2), .lt(BLT));  // open: gt, eq
  Comparator #(.width(32), .mode("unsigned")) comparator_5 (.a(_1), .b(_2), .lt(BLTU));  // open: gt, eq
  not not_1 (BNE, BEQ);
  not not_2 (BGE, BLT);
  not not_3 (BGEU, BLTU);
  Multiplexer #(.select(4), .width(32), .enable("false")) multiplexer_1 (
    .in0(SLL), .in1(SRL), .in2(SRA), .in3(ROR), .in4(ADD), .in5(SUB), .in6(SLT), .in7(SLTU), .in8(XOR),
    .in9(OR), .in10(AND), .in11(NOR), .in12(MUL), .in13(LUI), .in14(ADD), .out(Result), .sel(ALUOP));  // open: in15
  or or_2 (out_5, BEQ, BLT, BLTU);

  // Other names for the same wires on the sheet: _2_0_4[4:0] = _2[4:0]; _2_0_15[15:0] = _2[15:0]; LW[31:0] = ADD
endmodule

module ALU_Ctrl (
  input  [3:0] f,
  input  [4:0] opcode,
  output [3:0] ALUop
);

  ROM #(.addrWidth(9), .dataWidth(4)) rom_1 (.addr({opcode, f}), .data(ALUop));  // open: sel

  // Notes on the sheet:
  //   contents of rom_1 (hex, n*v repeats v):
  //   0 1 2 3 4 5 6 7 8 9 a b c 4*0 1 2 3 4 6 7 8 9 a b d 4*0 1 15*0 2 15*0 3 15*0 4 15*0 6 15*0 7 15*0 8
  //   15*0 9 15*0 a 15*0 d 15*0 d 31*0 e 15*0 e
endmodule

module Path_Ctrl (
  input  [5:0] opcode,
  output RegWr,
  output [1:0] AluSrc,
  output MemWr,
  output MemRd,
  output [1:0] WbData
);

  ROM #(.addrWidth(6), .dataWidth(7)) rom_1 (.addr(opcode), .data({WbData, MemRd, MemWr, AluSrc, RegWr}));  // open: sel

  // Notes on the sheet:
  //   contents of rom_1 (hex, n*v repeats v):
  //   1 4*3 5 5 5 5*3 45 35 e 4*0 2 2
endmodule

module PC_Ctrl (
  input  JALR,
  input  branchd,
  output [1:0] PCsrc,
  output Kill1,
  output Kill2
);

  wire [1:0] multiplexer_1_out;

  Multiplexer #(.width(2), .enable("false")) multiplexer_1 (
    .in0(2'b00), .in1(2'b01), .out(multiplexer_1_out), .sel(JALR));
  Multiplexer #(.width(2), .enable("false")) multiplexer_2 (
    .in0(multiplexer_1_out), .in1(2'b10), .out(PCsrc), .sel(branchd));
  or or_1 (Kill1, JALR, branchd);

  assign Kill2 = branchd;
endmodule

module Register (
  input  [4:0] RA,
  input  [4:0] RB,
  input  [4:0] RW,
  input  [31:0] BusW,
  input  RegWrite,
  input  Clock,
  input  CLR,
  output [31:0] BusA,
  output [31:0] BusB
);

  wire decoder_1_out0, decoder_1_out1, decoder_1_out2, decoder_1_out3, decoder_1_out4, decoder_1_out5,
       decoder_1_out6, decoder_1_out7, decoder_1_out8, decoder_1_out9, decoder_1_out10, decoder_1_out11,
       decoder_1_out12, decoder_1_out13, decoder_1_out14, decoder_1_out15, decoder_1_out16, decoder_1_out17,
       decoder_1_out18, decoder_1_out19, decoder_1_out20, decoder_1_out21, decoder_1_out22, decoder_1_out23,
       decoder_1_out24, decoder_1_out25, decoder_1_out26, decoder_1_out27, decoder_1_out28, decoder_1_out29,
       decoder_1_out30, decoder_1_out31, decoder_2_out0, decoder_2_out1, decoder_2_out2, decoder_2_out3,
       decoder_2_out4, decoder_2_out5, decoder_2_out6, decoder_2_out7, decoder_2_out8, decoder_2_out9,
       decoder_2_out10, decoder_2_out11, decoder_2_out12, decoder_2_out13, decoder_2_out14, decoder_2_out15,
       decoder_2_out16, decoder_2_out17, decoder_2_out18, decoder_2_out19, decoder_2_out20, decoder_2_out21,
       decoder_2_out22, decoder_2_out23, decoder_2_out24, decoder_2_out25, decoder_2_out26, decoder_2_out27,
       decoder_2_out28, decoder_2_out29, decoder_2_out30, decoder_2_out31, decoder_3_out0, decoder_3_out1,
       decoder_3_out2, decoder_3_out3, decoder_3_out4, decoder_3_out5, decoder_3_out6, decoder_3_out7,
       decoder_3_out8, decoder_3_out9, decoder_3_out10, decoder_3_out11, decoder_3_out12, decoder_3_out13,
       decoder_3_out14, decoder_3_out15, decoder_3_out16, decoder_3_out17, decoder_3_out18, decoder_3_out19,
       decoder_3_out20, decoder_3_out21, decoder_3_out22, decoder_3_out23, decoder_3_out24, decoder_3_out25,
       decoder_3_out26, decoder_3_out27, decoder_3_out28, decoder_3_out29, decoder_3_out30, decoder_3_out31,
       Reg1_out, Reg2_out, Reg3_out, Reg4_out, Reg5_out, Reg6_out, Reg7_out, Reg8_out, Reg9_out, Reg10_out,
       Reg11_out, Reg12_out, Reg13_out, Reg14_out, Reg15_out, Reg16_out, Reg17_out, Reg18_out, Reg19_out,
       Reg20_out, Reg21_out, Reg22_out, Reg23_out, Reg24_out, Reg25_out, Reg26_out, Reg27_out, Reg28_out,
       Reg29_out, Reg30_out, Reg31_out;
  wire [31:0] RE1, RE2, RE3, RE4, RE5, RE6, RE7, RE8, RE9, RE10, RE11, RE12, RE13, RE14, RE15, RE16, RE17,
       RE18, RE19, RE20, RE21, RE22, RE23, RE24, RE25, RE26, RE27, RE28, RE29, RE30, RE31;

  Decoder #(.select(5)) decoder_1 (
    .out0(decoder_1_out0), .out1(decoder_1_out1), .out2(decoder_1_out2), .out3(decoder_1_out3),
    .out4(decoder_1_out4), .out5(decoder_1_out5), .out6(decoder_1_out6), .out7(decoder_1_out7),
    .out8(decoder_1_out8), .out9(decoder_1_out9), .out10(decoder_1_out10), .out11(decoder_1_out11),
    .out12(decoder_1_out12), .out13(decoder_1_out13), .out14(decoder_1_out14), .out15(decoder_1_out15),
    .out16(decoder_1_out16), .out17(decoder_1_out17), .out18(decoder_1_out18), .out19(decoder_1_out19),
    .out20(decoder_1_out20), .out21(decoder_1_out21), .out22(decoder_1_out22), .out23(decoder_1_out23),
    .out24(decoder_1_out24), .out25(decoder_1_out25), .out26(decoder_1_out26), .out27(decoder_1_out27),
    .out28(decoder_1_out28), .out29(decoder_1_out29), .out30(decoder_1_out30), .out31(decoder_1_out31),
    .sel(RW));  // open: en
  Register_part #(.width(32)) register_1 (.D(BusW), .en(Reg1_out), .Q(RE1), .clk(Clock), .clr(CLR));
  and Reg1 (Reg1_out, decoder_1_out1, RegWrite);
  Register_part #(.width(32)) register_2 (.D(BusW), .en(Reg2_out), .Q(RE2), .clk(Clock), .clr(CLR));
  and Reg2 (Reg2_out, decoder_1_out2, RegWrite);
  Register_part #(.width(32)) register_3 (.D(BusW), .en(Reg3_out), .Q(RE3), .clk(Clock), .clr(CLR));
  and Reg3 (Reg3_out, decoder_1_out3, RegWrite);
  Register_part #(.width(32)) register_4 (.D(BusW), .en(Reg4_out), .Q(RE4), .clk(Clock), .clr(CLR));
  and Reg4 (Reg4_out, decoder_1_out4, RegWrite);
  Register_part #(.width(32)) register_5 (.D(BusW), .en(Reg5_out), .Q(RE5), .clk(Clock), .clr(CLR));
  and Reg5 (Reg5_out, decoder_1_out5, RegWrite);
  Register_part #(.width(32)) register_6 (.D(BusW), .en(Reg6_out), .Q(RE6), .clk(Clock), .clr(CLR));
  and Reg6 (Reg6_out, decoder_1_out6, RegWrite);
  Register_part #(.width(32)) register_7 (.D(BusW), .en(Reg7_out), .Q(RE7), .clk(Clock), .clr(CLR));
  and Reg7 (Reg7_out, decoder_1_out7, RegWrite);
  Register_part #(.width(32)) register_8 (.D(BusW), .en(Reg23_out), .Q(RE23), .clk(Clock), .clr(CLR));
  and Reg23 (Reg23_out, decoder_1_out23, RegWrite);
  Register_part #(.width(32)) register_9 (.D(BusW), .en(Reg22_out), .Q(RE22), .clk(Clock), .clr(CLR));
  and Reg22 (Reg22_out, decoder_1_out22, RegWrite);
  Register_part #(.width(32)) register_10 (.D(BusW), .en(Reg21_out), .Q(RE21), .clk(Clock), .clr(CLR));
  and Reg21 (Reg21_out, decoder_1_out21, RegWrite);
  Register_part #(.width(32)) register_11 (.D(BusW), .en(Reg20_out), .Q(RE20), .clk(Clock), .clr(CLR));
  and Reg20 (Reg20_out, decoder_1_out20, RegWrite);
  Register_part #(.width(32)) register_12 (.D(BusW), .en(Reg19_out), .Q(RE19), .clk(Clock), .clr(CLR));
  and Reg19 (Reg19_out, decoder_1_out19, RegWrite);
  Register_part #(.width(32)) register_13 (.D(BusW), .en(Reg18_out), .Q(RE18), .clk(Clock), .clr(CLR));
  and Reg18 (Reg18_out, decoder_1_out18, RegWrite);
  Register_part #(.width(32)) register_14 (.D(BusW), .en(Reg17_out), .Q(RE17), .clk(Clock), .clr(CLR));
  and Reg17 (Reg17_out, decoder_1_out17, RegWrite);
  Register_part #(.width(32)) register_15 (.D(BusW), .en(Reg16_out), .Q(RE16), .clk(Clock), .clr(CLR));
  and Reg16 (Reg16_out, decoder_1_out16, RegWrite);
  Register_part #(.width(32)) register_16 (.D(BusW), .en(Reg8_out), .Q(RE8), .clk(Clock), .clr(CLR));
  Register_part #(.width(32)) register_17 (.D(BusW), .en(Reg9_out), .Q(RE9), .clk(Clock), .clr(CLR));
  Register_part #(.width(32)) register_18 (.D(BusW), .en(Reg10_out), .Q(RE10), .clk(Clock), .clr(CLR));
  Register_part #(.width(32)) register_19 (.D(BusW), .en(Reg11_out), .Q(RE11), .clk(Clock), .clr(CLR));
  Register_part #(.width(32)) register_20 (.D(BusW), .en(Reg12_out), .Q(RE12), .clk(Clock), .clr(CLR));
  Register_part #(.width(32)) register_21 (.D(BusW), .en(Reg13_out), .Q(RE13), .clk(Clock), .clr(CLR));
  Register_part #(.width(32)) register_22 (.D(BusW), .en(Reg14_out), .Q(RE14), .clk(Clock), .clr(CLR));
  Register_part #(.width(32)) register_23 (.D(BusW), .en(Reg15_out), .Q(RE15), .clk(Clock), .clr(CLR));
  Register_part #(.width(32)) register_24 (.D(BusW), .en(Reg31_out), .Q(RE31), .clk(Clock), .clr(CLR));
  Register_part #(.width(32)) register_25 (.D(BusW), .en(Reg30_out), .Q(RE30), .clk(Clock), .clr(CLR));
  Register_part #(.width(32)) register_26 (.D(BusW), .en(Reg29_out), .Q(RE29), .clk(Clock), .clr(CLR));
  Register_part #(.width(32)) register_27 (.D(BusW), .en(Reg28_out), .Q(RE28), .clk(Clock), .clr(CLR));
  Register_part #(.width(32)) register_28 (.D(BusW), .en(Reg27_out), .Q(RE27), .clk(Clock), .clr(CLR));
  Register_part #(.width(32)) register_29 (.D(BusW), .en(Reg26_out), .Q(RE26), .clk(Clock), .clr(CLR));
  Register_part #(.width(32)) register_30 (.D(BusW), .en(Reg25_out), .Q(RE25), .clk(Clock), .clr(CLR));
  Register_part #(.width(32)) register_31 (.D(BusW), .en(Reg24_out), .Q(RE24), .clk(Clock), .clr(CLR));
  and Reg8 (Reg8_out, decoder_1_out8, RegWrite);
  and Reg9 (Reg9_out, decoder_1_out9, RegWrite);
  and Reg10 (Reg10_out, decoder_1_out10, RegWrite);
  and Reg11 (Reg11_out, decoder_1_out11, RegWrite);
  and Reg12 (Reg12_out, decoder_1_out12, RegWrite);
  and Reg13 (Reg13_out, decoder_1_out13, RegWrite);
  and Reg14 (Reg14_out, decoder_1_out14, RegWrite);
  and Reg15 (Reg15_out, decoder_1_out15, RegWrite);
  and Reg31 (Reg31_out, decoder_1_out31, RegWrite);
  and Reg30 (Reg30_out, decoder_1_out30, RegWrite);
  and Reg29 (Reg29_out, decoder_1_out29, RegWrite);
  and Reg28 (Reg28_out, decoder_1_out28, RegWrite);
  and Reg27 (Reg27_out, decoder_1_out27, RegWrite);
  and Reg26 (Reg26_out, decoder_1_out26, RegWrite);
  and Reg25 (Reg25_out, decoder_1_out25, RegWrite);
  and Reg24 (Reg24_out, decoder_1_out24, RegWrite);
  assign BusA = decoder_2_out0 ? {32{1'b0}} : 32'bz;  // Controlled_Buffer controlled_buffer_1
  assign BusA = decoder_2_out1 ? RE1 : 32'bz;  // Controlled_Buffer controlled_buffer_2
  assign BusA = decoder_2_out2 ? RE2 : 32'bz;  // Controlled_Buffer controlled_buffer_3
  assign BusA = decoder_2_out3 ? RE3 : 32'bz;  // Controlled_Buffer controlled_buffer_4
  assign BusA = decoder_2_out4 ? RE4 : 32'bz;  // Controlled_Buffer controlled_buffer_5
  assign BusA = decoder_2_out5 ? RE5 : 32'bz;  // Controlled_Buffer controlled_buffer_6
  assign BusA = decoder_2_out6 ? RE6 : 32'bz;  // Controlled_Buffer controlled_buffer_7
  assign BusA = decoder_2_out7 ? RE7 : 32'bz;  // Controlled_Buffer controlled_buffer_8
  assign BusA = decoder_2_out8 ? RE8 : 32'bz;  // Controlled_Buffer controlled_buffer_9
  assign BusA = decoder_2_out9 ? RE9 : 32'bz;  // Controlled_Buffer controlled_buffer_10
  assign BusA = decoder_2_out10 ? RE10 : 32'bz;  // Controlled_Buffer controlled_buffer_11
  assign BusA = decoder_2_out11 ? RE11 : 32'bz;  // Controlled_Buffer controlled_buffer_12
  assign BusA = decoder_2_out12 ? RE12 : 32'bz;  // Controlled_Buffer controlled_buffer_13
  assign BusA = decoder_2_out13 ? RE13 : 32'bz;  // Controlled_Buffer controlled_buffer_14
  assign BusA = decoder_2_out14 ? RE14 : 32'bz;  // Controlled_Buffer controlled_buffer_15
  assign BusA = decoder_2_out15 ? RE15 : 32'bz;  // Controlled_Buffer controlled_buffer_16
  assign BusA = decoder_2_out16 ? RE16 : 32'bz;  // Controlled_Buffer controlled_buffer_17
  Decoder #(.select(5)) decoder_2 (
    .out0(decoder_2_out0), .out1(decoder_2_out1), .out2(decoder_2_out2), .out3(decoder_2_out3),
    .out4(decoder_2_out4), .out5(decoder_2_out5), .out6(decoder_2_out6), .out7(decoder_2_out7),
    .out8(decoder_2_out8), .out9(decoder_2_out9), .out10(decoder_2_out10), .out11(decoder_2_out11),
    .out12(decoder_2_out12), .out13(decoder_2_out13), .out14(decoder_2_out14), .out15(decoder_2_out15),
    .out16(decoder_2_out16), .out17(decoder_2_out17), .out18(decoder_2_out18), .out19(decoder_2_out19),
    .out20(decoder_2_out20), .out21(decoder_2_out21), .out22(decoder_2_out22), .out23(decoder_2_out23),
    .out24(decoder_2_out24), .out25(decoder_2_out25), .out26(decoder_2_out26), .out27(decoder_2_out27),
    .out28(decoder_2_out28), .out29(decoder_2_out29), .out30(decoder_2_out30), .out31(decoder_2_out31),
    .sel(RA));  // open: en
  assign BusA = decoder_2_out17 ? RE17 : 32'bz;  // Controlled_Buffer controlled_buffer_18
  assign BusA = decoder_2_out18 ? RE18 : 32'bz;  // Controlled_Buffer controlled_buffer_19
  assign BusA = decoder_2_out19 ? RE19 : 32'bz;  // Controlled_Buffer controlled_buffer_20
  assign BusA = decoder_2_out20 ? RE20 : 32'bz;  // Controlled_Buffer controlled_buffer_21
  assign BusA = decoder_2_out21 ? RE21 : 32'bz;  // Controlled_Buffer controlled_buffer_22
  assign BusA = decoder_2_out22 ? RE22 : 32'bz;  // Controlled_Buffer controlled_buffer_23
  assign BusA = decoder_2_out23 ? RE23 : 32'bz;  // Controlled_Buffer controlled_buffer_24
  assign BusA = decoder_2_out24 ? RE24 : 32'bz;  // Controlled_Buffer controlled_buffer_25
  Controlled_Buffer #(.width(32)) controlled_buffer_26 (.in(RE25), .en(decoder_2_out25));  // open: out
  assign BusA = decoder_2_out26 ? RE26 : 32'bz;  // Controlled_Buffer controlled_buffer_27
  assign BusA = decoder_2_out27 ? RE27 : 32'bz;  // Controlled_Buffer controlled_buffer_28
  assign BusA = decoder_2_out28 ? RE28 : 32'bz;  // Controlled_Buffer controlled_buffer_29
  assign BusA = decoder_2_out29 ? RE29 : 32'bz;  // Controlled_Buffer controlled_buffer_30
  assign BusA = decoder_2_out30 ? RE30 : 32'bz;  // Controlled_Buffer controlled_buffer_31
  assign BusA = decoder_2_out31 ? RE31 : 32'bz;  // Controlled_Buffer controlled_buffer_32
  assign BusB = decoder_3_out0 ? {32{1'b0}} : 32'bz;  // Controlled_Buffer controlled_buffer_33
  assign BusB = decoder_3_out1 ? RE1 : 32'bz;  // Controlled_Buffer controlled_buffer_34
  assign BusB = decoder_3_out2 ? RE2 : 32'bz;  // Controlled_Buffer controlled_buffer_35
  assign BusB = decoder_3_out3 ? RE3 : 32'bz;  // Controlled_Buffer controlled_buffer_36
  assign BusB = decoder_3_out4 ? RE4 : 32'bz;  // Controlled_Buffer controlled_buffer_37
  assign BusB = decoder_3_out5 ? RE5 : 32'bz;  // Controlled_Buffer controlled_buffer_38
  assign BusB = decoder_3_out6 ? RE6 : 32'bz;  // Controlled_Buffer controlled_buffer_39
  assign BusB = decoder_3_out7 ? RE7 : 32'bz;  // Controlled_Buffer controlled_buffer_40
  assign BusB = decoder_3_out8 ? RE8 : 32'bz;  // Controlled_Buffer controlled_buffer_41
  assign BusB = decoder_3_out9 ? RE9 : 32'bz;  // Controlled_Buffer controlled_buffer_42
  assign BusB = decoder_3_out10 ? RE10 : 32'bz;  // Controlled_Buffer controlled_buffer_43
  assign BusB = decoder_3_out11 ? RE11 : 32'bz;  // Controlled_Buffer controlled_buffer_44
  assign BusB = decoder_3_out12 ? RE12 : 32'bz;  // Controlled_Buffer controlled_buffer_45
  assign BusB = decoder_3_out13 ? RE13 : 32'bz;  // Controlled_Buffer controlled_buffer_46
  assign BusB = decoder_3_out14 ? RE14 : 32'bz;  // Controlled_Buffer controlled_buffer_47
  assign BusB = decoder_3_out15 ? RE15 : 32'bz;  // Controlled_Buffer controlled_buffer_48
  assign BusB = decoder_3_out16 ? RE16 : 32'bz;  // Controlled_Buffer controlled_buffer_49
  assign BusB = decoder_3_out17 ? RE17 : 32'bz;  // Controlled_Buffer controlled_buffer_50
  Decoder #(.select(5)) decoder_3 (
    .out0(decoder_3_out0), .out1(decoder_3_out1), .out2(decoder_3_out2), .out3(decoder_3_out3),
    .out4(decoder_3_out4), .out5(decoder_3_out5), .out6(decoder_3_out6), .out7(decoder_3_out7),
    .out8(decoder_3_out8), .out9(decoder_3_out9), .out10(decoder_3_out10), .out11(decoder_3_out11),
    .out12(decoder_3_out12), .out13(decoder_3_out13), .out14(decoder_3_out14), .out15(decoder_3_out15),
    .out16(decoder_3_out16), .out17(decoder_3_out17), .out18(decoder_3_out18), .out19(decoder_3_out19),
    .out20(decoder_3_out20), .out21(decoder_3_out21), .out22(decoder_3_out22), .out23(decoder_3_out23),
    .out24(decoder_3_out24), .out25(decoder_3_out25), .out26(decoder_3_out26), .out27(decoder_3_out27),
    .out28(decoder_3_out28), .out29(decoder_3_out29), .out30(decoder_3_out30), .out31(decoder_3_out31),
    .sel(RB));  // open: en
  assign BusB = decoder_3_out18 ? RE18 : 32'bz;  // Controlled_Buffer controlled_buffer_51
  assign BusB = decoder_3_out19 ? RE19 : 32'bz;  // Controlled_Buffer controlled_buffer_52
  assign BusB = decoder_3_out20 ? RE20 : 32'bz;  // Controlled_Buffer controlled_buffer_53
  assign BusB = decoder_3_out21 ? RE21 : 32'bz;  // Controlled_Buffer controlled_buffer_54
  assign BusB = decoder_3_out22 ? RE22 : 32'bz;  // Controlled_Buffer controlled_buffer_55
  assign BusB = decoder_3_out23 ? RE23 : 32'bz;  // Controlled_Buffer controlled_buffer_56
  assign BusB = decoder_3_out24 ? RE24 : 32'bz;  // Controlled_Buffer controlled_buffer_57
  Controlled_Buffer #(.width(32)) controlled_buffer_58 (.in(RE25), .en(decoder_3_out25));  // open: out
  assign BusB = decoder_3_out26 ? RE26 : 32'bz;  // Controlled_Buffer controlled_buffer_59
  assign BusB = decoder_3_out27 ? RE27 : 32'bz;  // Controlled_Buffer controlled_buffer_60
  assign BusB = decoder_3_out28 ? RE28 : 32'bz;  // Controlled_Buffer controlled_buffer_61
  assign BusB = decoder_3_out29 ? RE29 : 32'bz;  // Controlled_Buffer controlled_buffer_62
  assign BusB = decoder_3_out30 ? RE30 : 32'bz;  // Controlled_Buffer controlled_buffer_63
  assign BusB = decoder_3_out31 ? RE31 : 32'bz;  // Controlled_Buffer controlled_buffer_64
  // also tied to GND on the sheet: decoder_1_out0
endmodule

module Forward_Hazard (
  input  [4:0] rd2,
  input  [4:0] rd3,
  input  [4:0] rd4,
  input  EXMEMRD,
  input  EXWR,
  input  MEMWR,
  input  WBWR,
  input  [5:0] opcode,
  input  Branch,
  input  [4:0] rs1,
  input  [4:0] rs2,
  output Stall,
  output [1:0] FA,
  output JALR,
  output [1:0] FB,
  output branchd
);

  wire and_8_out, and_9_out, and_10_out, and_11_out, and_12_out, and_13_out, BEQ, BGE, BGEU, BLT, BLTU, BNE,
       comparator_1_eq, comparator_2_eq, comparator_3_eq, comparator_4_eq, comparator_5_eq, comparator_6_eq,
       not_1_out, not_2_out, not_3_out, or_1_out, or_2_out, or_3_out, or_4_out, or_5_out, or_6_out, or_7_out;
  wire [2:0] and_1_out, and_4_out;

  or or_1 (or_1_out, rs1[0], rs1[1], rs1[2], rs1[3], rs1[4]);
  Comparator #(.width(5)) comparator_1 (.a(rs1), .b(rd2), .eq(comparator_1_eq));  // open: gt, lt
  or or_2 (or_2_out, rs1[0], rs1[1], rs1[2], rs1[3], rs1[4]);
  Comparator #(.width(5)) comparator_2 (.a(rs1), .b(rd3), .eq(comparator_2_eq));  // open: gt, lt
  or or_3 (or_3_out, rs1[0], rs1[1], rs1[2], rs1[3], rs1[4]);
  Comparator #(.width(5)) comparator_3 (.a(rs1), .b(rd4), .eq(comparator_3_eq));  // open: gt, lt
  or or_4 (or_4_out, rs2[0], rs2[1], rs2[2], rs2[3], rs2[4]);
  Comparator #(.width(5)) comparator_4 (.a(rs2), .b(rd2), .eq(comparator_4_eq));  // open: gt, lt
  or or_5 (or_5_out, rs2[0], rs2[1], rs2[2], rs2[3], rs2[4]);
  Comparator #(.width(5)) comparator_5 (.a(rs2), .b(rd3), .eq(comparator_5_eq));  // open: gt, lt
  or or_6 (or_6_out, rs2[0], rs2[1], rs2[2], rs2[3], rs2[4]);
  Comparator #(.width(5)) comparator_6 (.a(rs2), .b(rd4), .eq(comparator_6_eq));  // open: gt, lt
  and and_1 (and_1_out[0], or_1_out, EXWR, comparator_1_eq);
  and and_2 (and_1_out[1], or_2_out, MEMWR, comparator_2_eq);
  and and_3 (and_1_out[2], or_3_out, WBWR, comparator_3_eq);
  and and_4 (and_4_out[0], or_4_out, EXWR, comparator_4_eq);
  and and_5 (and_4_out[1], or_5_out, MEMWR, comparator_5_eq);
  and and_6 (and_4_out[2], or_6_out, WBWR, comparator_6_eq);
  Multiplexer #(.select(3), .width(2), .enable("false")) multiplexer_1 (
    .in0(2'b00), .in1(2'b01), .in2(2'b10), .in3(2'b01), .in4(2'b11), .in5(2'b01), .in6(2'b10), .in7(2'b01),
    .out(FA), .sel(and_1_out));
  Multiplexer #(.select(3), .width(2), .enable("false")) multiplexer_2 (
    .in0(2'b00), .in1(2'b01), .in2(2'b10), .in3(2'b01), .in4(2'b11), .in5(2'b01), .in6(2'b10), .in7(2'b01),
    .out(FB), .sel(and_4_out));
  or or_7 (or_7_out, FA[0], FB[0]);
  and and_7 (Stall, or_7_out, EXMEMRD);
  and and_8 (and_8_out, BEQ, Branch);
  not not_1 (not_1_out, Branch);
  and and_9 (and_9_out, BNE, not_1_out);
  and and_10 (and_10_out, BLT, Branch);
  not not_2 (not_2_out, Branch);
  and and_11 (and_11_out, BGE, not_2_out);
  and and_12 (and_12_out, BLTU, Branch);
  Decoder #(.select(5), .enable("false")) decoder_1 (
    .out13(JALR), .out16(BEQ), .out17(BNE), .out18(BLT), .out19(BGE), .out20(BLTU), .out21(BGEU),
    .sel(opcode[4:0]));  // open: out0, out1, out2, out3, out4, out5, out6, out7, out8, out9, out10, out11, out12, out14, out15, out22, out23, out24, out25, out26, out27, out28, out29, out30, out31
  not not_3 (not_3_out, Branch);
  and and_13 (and_13_out, BGEU, not_3_out);
  or or_8 (branchd, and_13_out, and_12_out, and_11_out, and_10_out, and_9_out, and_8_out);
endmodule
