// Logisim project ALU.circ as structural Verilog: 1 circuit, main circuit ALU
module ALU (
  input  [3:0] ALUOP,
  input  [31:0] A,
  input  [31:0] B,
  output [31:0] ALU_OUTPUT,
  output ZeroFlag
);

  wire and_3_out, BEQ, BGEU, BGT, BLT, BLTU, BNE, comparator_1_eq, comparator_1_gt;
  wire [31:0] adder_1_out, AND_2_out, bit_extender_1_out, bit_extender_2_out, multiplier_1_out, NOR_out,
       or_1_out, shifter_1_out, shifter_2_out, shifter_3_out, shifter_4_out, subtractor_1_out, xor_1_out;

  // Probe on A
  // Probe on B
  Shifter #(.width(32), .shift("rr")) shifter_1 (.in(A), .\dist (B[4:0]), .out(shifter_1_out));
  Shifter #(.width(32), .shift("ar")) shifter_2 (.in(A), .\dist (B[4:0]), .out(shifter_2_out));
  Adder #(.width(32)) adder_1 (.a(A), .b(B), .out(adder_1_out));  // open: cin, cout
  Comparator #(.width(32), .mode("unsigned")) comparator_1 (
    .a(A), .b(B), .gt(comparator_1_gt), .eq(comparator_1_eq), .lt(BLTU));
  Subtractor #(.width(32)) subtractor_1 (.a(A), .b(B), .out(subtractor_1_out));  // open: bin, bout
  not not_1 (BNE, BEQ);
  Comparator #(.width(32)) comparator_2 (.a(A), .b(B), .gt(BGT), .eq(BEQ), .lt(BLT));
  and and_1 (BGEU, comparator_1_gt, comparator_1_eq);
  assign xor_1_out = A ^ B;  // XOR_Gate xor_1, 32 bits wide
  assign or_1_out = A | B;  // OR_Gate or_1, 32 bits wide
  assign AND_2_out = A & B;  // AND_Gate AND_2, 32 bits wide
  assign NOR_out = ~(A | B);  // NOR_Gate NOR, 32 bits wide
  Multiplier #(.width(32)) multiplier_1 (.a(A), .b(B), .out(multiplier_1_out));  // open: cin, cout
  Shifter #(.width(32), .shift("lr")) shifter_3 (.in(A), .\dist (B[4:0]), .out(shifter_3_out));
  assign bit_extender_1_out = {{31{1'b0}}, BLT};  // Bit_Extender bit_extender_1
  assign bit_extender_2_out = {{31{1'b0}}, BLTU};  // Bit_Extender bit_extender_2
  Shifter #(.width(32)) shifter_4 (.in(A), .\dist (B[4:0]), .out(shifter_4_out));
  Multiplexer #(.select(4), .width(32), .enable("false")) multiplexer_1 (
    .in0(shifter_4_out), .in1(shifter_3_out), .in2(shifter_2_out), .in3(shifter_1_out), .in4(adder_1_out),
    .in5(subtractor_1_out), .in6(bit_extender_1_out), .in7(bit_extender_2_out), .in8(xor_1_out),
    .in9(or_1_out), .in10(AND_2_out), .in11(NOR_out), .in12(multiplier_1_out), .in13({B[15:0], {16{1'b0}}}),
    .out(ALU_OUTPUT), .sel(ALUOP));  // open: in14, in15
  and and_3 (and_3_out, BGT, BEQ);
  Multiplexer #(.select(3), .enable("false")) multiplexer_2 (
    .in0(BEQ), .in1(BNE), .in2(BLT), .in3(and_3_out), .in4(BLTU), .in5(BGEU), .out(ZeroFlag), .sel(ALUOP[2:0]));  // open: in6, in7

  // Other names for the same wires on the sheet: BranchSelect[2:0] = ALUOP[2:0]

  // Notes on the sheet:
  //   ALUOP
  //   LUI
  //   ROR
  //   SLTU
  //   SRA
  //   ADD
  //   SLT
  //   SRL
  //   SUB
  //   XOR
  //   OR
  //   MUL
  //   SLL
  //   OUTPUT
endmodule
