// Logisim project ALUCtrl.circ as structural Verilog: 1 circuit, main circuit ALUCtrl
module ALUCtrl (
  input  [10:0] FunctoinCode,
  input  [5:0] OpCode,
  output [3:0] ALUOp
);

  wire comparator_1_eq;
  wire [3:0] rom_1_data;

  ROM #(.addrWidth(5), .dataWidth(4)) rom_1 (.addr(OpCode[4:0]), .data(rom_1_data));  // open: sel
  Comparator #(.width(6)) comparator_1 (.a(OpCode), .b({6{1'b0}}), .eq(comparator_1_eq));  // open: gt, lt
  Multiplexer #(.width(4), .enable("false")) multiplexer_1 (
    .in0(rom_1_data), .in1(FunctoinCode[3:0]), .out(ALUOp), .sel(comparator_1_eq));

  // Other names for the same wires on the sheet: ALUOpR[3:0] = FunctoinCode[3:0]; OpCodeALU[4:0] = OpCode[4:0]

  // Notes on the sheet:
  //   contents of rom_1 (hex, n*v repeats v):
  //   0 0 1 2 3 4 6 7 8 9 a b d 0 4 4 0 1 2 3 4 5
endmodule
