// Logisim project singleCycleCPU.circ as structural Verilog: 3 circuits, main circuit main
module main (
);

  wire clock_1_out, clock_2_out, MemoryRead, MemoryWrite, regWrite, Zero;
  wire [1:0] BusBSrc, BusWSrc, pcctrl_1_out_3;
  wire [3:0] ALUOP;
  wire [4:0] imm16, rd___imm5l, rs1;
  wire [5:0] opcode;
  wire [10:0] f___imm11u;
  wire [19:0] bit_extender_1_out, Branch_Target, BTarget, Jump_Target, multiplexer_1_out, PC___1, PC_q;
  wire [31:0] alu_1_alu_output, bit_extender_2_out, bit_extender_3_out, bit_extender_4_out,
       bit_extender_6_out, multiplexer_2_out, Ra, ram_1_data, Rb, WBbusW;

  assign bit_extender_1_out = {{4{f___imm11u[10]}}, {f___imm11u, imm16}};  // Bit_Extender bit_extender_1
  Adder #(.width(20)) adder_1 (.a(20'h1), .b(PC_q), .out(PC___1));  // open: cin, cout
  Multiplexer #(.select(2), .width(20), .enable("false")) multiplexer_1 (
    .in0(PC___1), .in1(Jump_Target), .in2(Branch_Target), .in3({20{1'b0}}), .out(multiplexer_1_out),
    .sel(pcctrl_1_out_3));
  PcCtrl pcctrl_1 (.OpCode(opcode), .out_3(pcctrl_1_out_3), .ZeroFlag(Zero));
  Adder #(.width(20)) adder_2 (.a(bit_extender_1_out), .b(Ra[19:0]), .out(Jump_Target));  // open: cin, cout
  Register #(.width(20)) PC (.D(multiplexer_1_out), .Q(PC_q), .clk(clock_1_out));  // open: en, clr
  Clock clock_1 (.out(clock_1_out));
  Adder #(.width(20)) adder_3 (.a(PC_q), .b(BTarget), .out(Branch_Target));  // open: cin, cout
  ctrl_unit ctrl_unit_1 (
    .in_1(opcode), .MemroyWrite(MemoryWrite), .BusWSrc(BusWSrc), .RegWrite(regWrite), .BusBSrc(BusBSrc),
    .MemoryRead(MemoryRead));
  ROM #(.addrWidth(20), .dataWidth(32)) rom_1 (
    .addr(PC_q), .data({f___imm11u, imm16, rs1, rd___imm5l, opcode}), .sel(1'b1));
  // Probe on {f___imm11u, imm16}
  // Probe on opcode
  // Probe on f___imm11u
  // Probe on rd___imm5l
  // Probe on rs1
  // Probe on imm16
  // Probe on WBbusW
  assign bit_extender_2_out = {{16{f___imm11u[10]}}, {f___imm11u, imm16}};  // Bit_Extender bit_extender_2
  assign bit_extender_3_out = {{16{1'b0}}, {f___imm11u, imm16}};  // Bit_Extender bit_extender_3
  register_file register_file_1 (
    .RA(rs1), .RB(imm16), .RegWrite(regWrite), .RW(rd___imm5l), .BusW(WBbusW), .BusB(Rb), .BusA(Ra));
  assign bit_extender_4_out = {{16{f___imm11u[10]}}, {f___imm11u, rd___imm5l}};  // Bit_Extender bit_extender_4
  // Probe on Ra
  Multiplexer #(.select(2), .width(32), .enable("false")) multiplexer_2 (
    .in0(Rb), .in1(bit_extender_2_out), .in2(bit_extender_3_out), .in3(bit_extender_4_out),
    .out(multiplexer_2_out), .sel(BusBSrc));
  // Probe on BusBSrc
  assign BTarget = {{4{f___imm11u[10]}}, {f___imm11u, rd___imm5l}};  // Bit_Extender bit_extender_5
  // Probe on ALUOP
  // Probe on bit_extender_4_out
  ALU alu_1 (.A(Ra), .ALUOP(ALUOP), .ALU_OUTPUT(alu_1_alu_output), .B(multiplexer_2_out), .ZeroFlag(Zero));
  // Probe on alu_1_alu_output
  ALUCtrl aluctrl_1 (.FunctoinCode(f___imm11u), .OpCode(opcode), .ALUOp(ALUOP));
  assign bit_extender_6_out = {{12{1'b0}}, PC___1};  // Bit_Extender bit_extender_6
  // Probe on MemoryWrite
  Clock clock_2 (.out(clock_2_out));
  RAM #(.addrWidth(20), .dataWidth(32), .bus("separate")) ram_1 (
    .addr(alu_1_alu_output[19:0]), .din(Rb), .data(ram_1_data), .str(MemoryWrite), .clk(clock_2_out),
    .ld(MemoryRead));  // open: sel, clr
  // Probe on MemoryRead
  Multiplexer #(.select(2), .width(32), .enable("false")) multiplexer_3 (
    .in0(alu_1_alu_output), .in1(ram_1_data), .in2(bit_extender_6_out), .in3({32{1'b0}}), .out(WBbusW),
    .sel(BusWSrc));
  // Probe on BusWSrc

  // Other names for the same wires on the sheet: rs2[4:0] = imm16; imm16[15:5] = f___imm11u

  // Notes on the sheet:
  //   contents of rom_1 (hex, n*v repeats v):
  //   f0849 11089 18c9 202109 2949 419d0 14111c0 10842 3890 12945 118c5 5000d 5000f 4e
  //   busB
  //   imm16s
  //   imm16z
  //   imm11,5s
  //   A
endmodule

module ctrl_unit (
  input  [5:0] in_1,
  output RegWrite,
  output [1:0] BusBSrc,
  output MemroyWrite,
  output MemoryRead,
  output [1:0] BusWSrc
);

  ROM #(.addrWidth(6), .dataWidth(7)) rom_1 (
    .addr(in_1), .data({RegWrite, BusBSrc, MemroyWrite, MemoryRead, BusWSrc}));  // open: sel

  // Notes on the sheet:
  //   opCode
  //   contents of rom_1 (hex, n*v repeats v):
  //   40 4*60 50 50 50 4*60 50 52 55 38
endmodule

module PcCtrl (
  input  [5:0] OpCode,
  input  ZeroFlag,
  output [1:0] out_3
);

  and and_1 (out_3[1], ZeroFlag, OpCode[4]);
  and and_2 (out_3[0], OpCode[3], OpCode[2], ~OpCode[1], OpCode[0]);  // AND_Gate
endmodule
